// Logisim project tennis.circ as structural Verilog
module main (
  input  in_1
);

  wire clock_1_out, undriven, undriven_2;
  wire [4:0] controller_1_out_7, controller_1_out_8, controller_1_out_9, controller_1_out_10,
       controller_1_out_11, display_1_out_14, display_1_out_15, display_1_out_16, display_1_out_17,
       display_1_out_18, display_2_out_14, display_2_out_15, display_2_out_16, display_2_out_17,
       display_2_out_18, display_3_out_14, display_3_out_15, display_3_out_16, display_3_out_17,
       display_3_out_18;
  wire [6:0] keyboard_1_data;
  wire [7:0] controller_1_out_5, controller_1_out_6;
  wire [31:0] display_1_out_6, display_1_out_7, display_1_out_8, display_1_out_9, display_1_out_10,
       display_1_out_11, display_1_out_12, display_1_out_13, display_2_out_6, display_2_out_7,
       display_2_out_8, display_2_out_9, display_2_out_10, display_2_out_11, display_2_out_12,
       display_2_out_13, display_3_out_6, display_3_out_7, display_3_out_8, display_3_out_9,
       display_3_out_10, display_3_out_11, display_3_out_12, display_3_out_13, display_4_out_6,
       display_4_out_7, display_4_out_8, display_4_out_9, display_4_out_10, display_4_out_11,
       display_4_out_12, display_4_out_13;

  Keyboard keyboard_1 (.clk(clock_1_out), .data(keyboard_1_data));  // open: re, clr, avail
  Clock clock_1 (.out(clock_1_out));
  _7_Segment_Display u_7_segment_display_1 (.b(undriven), .dp(undriven_2));  // open: g, f, a, e, d, c
  _7_Segment_Display u_7_segment_display_2 (.g(undriven), .e(undriven_2));  // open: f, a, b, d, c, dp
  DotMatrix #(.matrixcols(32), .matrixrows(32)) dotmatrix_1 (
    .col0(display_1_out_6), .col1(display_1_out_7), .col2(display_1_out_8), .col3(display_1_out_9),
    .col4(display_1_out_10), .col5(display_1_out_11), .col6(display_1_out_12), .col7(display_1_out_13),
    .col8(display_2_out_6), .col9(display_2_out_7), .col10(display_2_out_8), .col11(display_2_out_9),
    .col12(display_2_out_10), .col13(display_2_out_11), .col14(display_2_out_12), .col15(display_2_out_13),
    .col16(display_3_out_6), .col17(display_3_out_7), .col18(display_3_out_8), .col19(display_3_out_9),
    .col20(display_3_out_10), .col21(display_3_out_11), .col22(display_3_out_12), .col23(display_3_out_13),
    .col24(display_4_out_6), .col25(display_4_out_7), .col26(display_4_out_8), .col27(display_4_out_9),
    .col28(display_4_out_10), .col29(display_4_out_11), .col30(display_4_out_12), .col31(display_4_out_13));
  controller controller_1 (
    .in_1(in_1), .keyboard_in(keyboard_1_data), .out_7(controller_1_out_7), .out_8(controller_1_out_8),
    .out_9(controller_1_out_9), .out_10(controller_1_out_10), .out_11(controller_1_out_11),
    .out_5(controller_1_out_5), .out_6(controller_1_out_6));  // open: old_vx, in_4
  display display_1 (
    .in_1(controller_1_out_7), .in_2(controller_1_out_8), .in_3(controller_1_out_9),
    .in_4(controller_1_out_10), .in_5(controller_1_out_11), .out_14(display_1_out_14),
    .out_15(display_1_out_15), .out_16(display_1_out_16), .out_17(display_1_out_17),
    .out_18(display_1_out_18), .out_8(display_1_out_8), .out_6(display_1_out_6), .out_7(display_1_out_7),
    .out_9(display_1_out_9), .out_10(display_1_out_10), .out_11(display_1_out_11), .out_12(display_1_out_12),
    .out_13(display_1_out_13));
  display display_2 (
    .in_1(display_1_out_14), .in_2(display_1_out_15), .in_3(display_1_out_16), .in_4(display_1_out_17),
    .in_5(display_1_out_18), .out_14(display_2_out_14), .out_15(display_2_out_15), .out_16(display_2_out_16),
    .out_17(display_2_out_17), .out_18(display_2_out_18), .out_8(display_2_out_8), .out_6(display_2_out_6),
    .out_7(display_2_out_7), .out_9(display_2_out_9), .out_10(display_2_out_10), .out_11(display_2_out_11),
    .out_12(display_2_out_12), .out_13(display_2_out_13));
  display display_3 (
    .in_1(display_2_out_14), .in_2(display_2_out_15), .in_3(display_2_out_16), .in_4(display_2_out_17),
    .in_5(display_2_out_18), .out_14(display_3_out_14), .out_15(display_3_out_15), .out_16(display_3_out_16),
    .out_17(display_3_out_17), .out_18(display_3_out_18), .out_8(display_3_out_8), .out_6(display_3_out_6),
    .out_7(display_3_out_7), .out_9(display_3_out_9), .out_10(display_3_out_10), .out_11(display_3_out_11),
    .out_12(display_3_out_12), .out_13(display_3_out_13));
  _7_Segment_Display u_7_segment_display_3 ();  // open: g, f, a, b, e, d, c, dp
  display display_4 (
    .in_1(display_3_out_14), .in_2(display_3_out_15), .in_3(display_3_out_16), .in_4(display_3_out_17),
    .in_5(display_3_out_18), .out_8(display_4_out_8), .out_6(display_4_out_6), .out_7(display_4_out_7),
    .out_9(display_4_out_9), .out_10(display_4_out_10), .out_11(display_4_out_11), .out_12(display_4_out_12),
    .out_13(display_4_out_13));  // open: out_14, out_15, out_16, out_17, out_18
  _7_Segment_Display u_7_segment_display_4 ();  // open: g, f, a, b, e, d, c, dp
endmodule

module inc (
  input  [4:0] in_1,
  output [4:0] out_2
);

  Adder #(.width(5)) adder_1 (.a(in_1), .b(5'b00001), .out(out_2));  // open: cin, cout
endmodule

module display (
  input  [4:0] in_1,
  input  [4:0] in_2,
  input  [4:0] in_3,
  input  [4:0] in_4,
  input  [4:0] in_5,
  output [31:0] out_6,
  output [31:0] out_7,
  output [31:0] out_8,
  output [31:0] out_9,
  output [31:0] out_10,
  output [31:0] out_11,
  output [31:0] out_12,
  output [31:0] out_13,
  output [4:0] out_14,
  output [4:0] out_15,
  output [4:0] out_16,
  output [4:0] out_17,
  output [4:0] out_18
);

  wire _0, _1, _2, _3, _4, _5, _6, _7, comparator_1_eq, comparator_2_eq, comparator_3_eq;
  wire [4:0] divider_1_out, divider_1_rem;
  wire [31:0] controlled_buffer_2_out, l_bat32, multiplexer_1_out, multiplexer_2_out, multiplexer_3_out,
       multiplexer_4_out, multiplexer_5_out, multiplexer_6_out, multiplexer_7_out, multiplexer_8_out,
       pull_resistor_4_node, r_bat32, y32;

  assign out_6 = {32{1'b0}} | multiplexer_1_out;  // OR_Gate or_1, 32 bits wide
  Multiplexer #(.width(32)) multiplexer_1 (.in0({32{1'b0}}), .in1(y32), .out(multiplexer_1_out), .sel(_0));  // open: en
  Pull_Resistor pull_resistor_1 (.node(_0));
  Pull_Resistor pull_resistor_2 (.node(_1));
  assign out_7 = {32{1'b0}} | multiplexer_2_out;  // OR_Gate or_2, 32 bits wide
  Multiplexer #(.width(32)) multiplexer_2 (.in0({32{1'b0}}), .in1(y32), .out(multiplexer_2_out), .sel(_1));  // open: en
  Comparator #(.width(5), .mode("unsigned")) comparator_1 (
    .a(in_1), .b({5{1'b0}}), .eq(comparator_1_eq));  // open: gt, lt
  assign out_8 = {32{1'b0}} | multiplexer_3_out;  // OR_Gate or_3, 32 bits wide
  Multiplexer #(.width(32)) multiplexer_3 (.in0({32{1'b0}}), .in1(y32), .out(multiplexer_3_out), .sel(_2));  // open: en
  Pull_Resistor pull_resistor_3 (.node(_2));
  Pull_Resistor pull_resistor_4 (.node(pull_resistor_4_node));
  assign pull_resistor_4_node = comparator_1_eq ? l_bat32 : 32'bz;  // Controlled_Buffer controlled_buffer_1
  assign out_9 = {32{1'b0}} | pull_resistor_4_node | multiplexer_4_out;  // OR_Gate or_4, 32 bits wide
  Multiplexer #(.width(32)) multiplexer_4 (.in0({32{1'b0}}), .in1(y32), .out(multiplexer_4_out), .sel(_3));  // open: en
  Pull_Resistor pull_resistor_5 (.node(_3));
  Comparator #(.width(5), .mode("unsigned")) comparator_2 (
    .a(in_1), .b(5'b00011), .eq(comparator_2_eq));  // open: gt, lt
  inc inc_1 (.in_1(in_1), .out_2(out_14));
  assign out_10 = {32{1'b0}} | controlled_buffer_2_out | multiplexer_5_out;  // OR_Gate or_5, 32 bits wide
  Pull_Resistor pull_resistor_6 (.node(_4));
  assign controlled_buffer_2_out = comparator_2_eq ? r_bat32 : 32'bz;  // Controlled_Buffer controlled_buffer_2
  Pull_Resistor pull_resistor_7 (.node(controlled_buffer_2_out));
  Multiplexer #(.width(32)) multiplexer_5 (.in0({32{1'b0}}), .in1(y32), .out(multiplexer_5_out), .sel(_4));  // open: en
  assign out_11 = {32{1'b0}} | multiplexer_6_out;  // OR_Gate or_6, 32 bits wide
  Pull_Resistor pull_resistor_8 (.node(_5));
  Comparator #(.width(5)) comparator_3 (.a(in_1), .b(divider_1_out), .eq(comparator_3_eq));  // open: gt, lt
  Divider #(.width(5)) divider_1 (.a(in_2), .b(5'b01000), .out(divider_1_out), .rem(divider_1_rem));  // open: upper
  Multiplexer #(.width(32)) multiplexer_6 (.in0({32{1'b0}}), .in1(y32), .out(multiplexer_6_out), .sel(_5));  // open: en
  Shifter #(.width(32)) shifter_1 (.in(32'h1), .\dist (in_3), .out(y32));
  Shifter #(.width(32)) shifter_2 (.in(32'h7), .\dist (in_4), .out(l_bat32));
  Shifter #(.width(32)) shifter_3 (.in(32'h7), .\dist (in_5), .out(r_bat32));
  assign out_12 = {32{1'b0}} | multiplexer_7_out;  // OR_Gate or_7, 32 bits wide
  Pull_Resistor pull_resistor_9 (.node(_6));
  Decoder #(.select(3)) decoder_1 (
    .out0(_0), .out1(_1), .out2(_2), .out3(_3), .out4(_4), .out5(_5), .out6(_6), .out7(_7),
    .sel(divider_1_rem[2:0]), .en(comparator_3_eq));
  Multiplexer #(.width(32)) multiplexer_7 (.in0({32{1'b0}}), .in1(y32), .out(multiplexer_7_out), .sel(_6));  // open: en
  assign out_13 = {32{1'b0}} | multiplexer_8_out;  // OR_Gate or_8, 32 bits wide
  Multiplexer #(.width(32)) multiplexer_8 (.in0({32{1'b0}}), .in1(y32), .out(multiplexer_8_out), .sel(_7));  // open: en
  Pull_Resistor pull_resistor_10 (.node(_7));

  assign out_15 = in_2;
  assign out_16 = in_3;
  assign out_17 = in_4;
  assign out_18 = in_5;

  // Other names for the same wires on the sheet: l_bat[4:0] = in_4; r_bat[4:0] = in_5; y[4:0] = in_3
endmodule

module controller (
  input  in_1,
  input  [4:0] old_vx,
  input  [6:0] keyboard_in,
  input  [4:0] in_4,
  output [7:0] out_5,
  output [7:0] out_6,
  output [4:0] out_7,
  output [4:0] out_8,
  output [4:0] out_9,
  output [4:0] out_10,
  output [4:0] out_11
);

  wire aboba, and_1_out, and_2_out, and_3_out, clock, col, comparator_1_gt, comparator_1_lt, comparator_2_eq,
       comparator_3_eq, d_ff_1_q, d_ff_2_q, d_ff_3_q, d_ff_4_q, d_ff_5_q, nand_1_out, nand_2_out, not_2_out,
       not_4_out, not_5_out, not_6_out, not_7_out, not_8_out, p1g, p2g, \reg ;
  wire [1:0] keyboard_1_p2;
  wire [2:0] motion_1_new_speed, motion_2_new_speed, multiplexer_1_out, multiplexer_2_out, multiplexer_5_out,
       negator_1_out, register_2_q, register_3_q, vx_q, vy_q;
  wire [4:0] adder_1_out, controlled_buffer_1_out, register_1_q, subtractor_1_out;
  wire [7:0] motion_1_new_cords, motion_2_new_cords, multiplexer_3_out, multiplexer_4_out, multiplexer_6_out,
       multiplexer_7_out, x_q, y_q;

  Clock clock_1 (.out(aboba));
  Multiplexer #(.width(3)) multiplexer_1 (
    .in0(motion_2_new_speed), .in1(3'b001), .out(multiplexer_1_out), .sel(in_1));  // open: en
  Multiplexer #(.width(3)) multiplexer_2 (
    .in0(multiplexer_5_out), .in1(3'b010), .out(multiplexer_2_out), .sel(in_1));  // open: en
  Register #(.width(3)) vy (.D(multiplexer_1_out), .Q(vy_q), .clk(clock));  // open: en, clr
  // ai_keyboard keyboard_1: pin names not known; wires that end beside it: keyboard_in, keyboard_1_p2
  Multiplexer #(.width(8)) multiplexer_3 (
    .in0(multiplexer_7_out), .in1({8{1'b0}}), .out(multiplexer_3_out), .sel(in_1));  // open: en
  Register y (.D(multiplexer_4_out), .Q(y_q), .clk(clock));  // open: en, clr
  Multiplexer #(.width(8)) multiplexer_4 (
    .in0(multiplexer_6_out), .in1({8{1'b0}}), .out(multiplexer_4_out), .sel(in_1));  // open: en
  Comparator #(.width(2)) comparator_1 (
    .a(keyboard_1_p2), .b(2'b00), .gt(comparator_1_gt), .lt(comparator_1_lt));  // open: eq
  Register #(.width(5)) register_1 (.D(controlled_buffer_1_out), .Q(register_1_q), .clk(clock));  // open: en, clr
  Register x (.D(multiplexer_3_out), .Q(x_q), .clk(clock));  // open: en, clr
  Register #(.width(3)) vx (.D(multiplexer_2_out), .Q(vx_q), .clk(clock));  // open: en, clr
  Multiplexer #(.width(3)) multiplexer_5 (
    .in0(motion_1_new_speed), .in1(negator_1_out), .out(multiplexer_5_out), .sel(col));  // open: en
  assign controlled_buffer_1_out = comparator_1_gt ? subtractor_1_out : 5'bz;  // Controlled_Buffer controlled_buffer_1
  Subtractor #(.width(5)) subtractor_1 (.a(register_1_q), .b(5'b00001), .out(subtractor_1_out));  // open: bin, bout
  assign controlled_buffer_1_out = comparator_1_lt ? adder_1_out : 5'bz;  // Controlled_Buffer controlled_buffer_2
  Adder #(.width(5)) adder_1 (.a(5'b00001), .b(register_1_q), .out(adder_1_out));  // open: cin, cout
  motion motion_1 (
    .coord(x_q), .speed(vx_q), .p1goal(p1g), .p2goal(p2g), .new_cords(motion_1_new_cords),
    .new_speed(motion_1_new_speed));
  Negator #(.width(3)) negator_1 (.in(motion_1_new_speed), .out(negator_1_out));
  Multiplexer #(.width(8)) multiplexer_6 (
    .in0(motion_2_new_cords), .in1(y_q), .out(multiplexer_6_out), .sel(col));  // open: en
  motion motion_2 (
    .coord(y_q), .speed(vy_q), .new_cords(motion_2_new_cords), .new_speed(motion_2_new_speed));  // open: p1goal, p2goal
  Comparator #(.width(5)) comparator_2 (.a({5{1'b0}}), .b(register_1_q), .eq(comparator_2_eq));  // open: gt, lt
  Comparator #(.width(5)) comparator_3 (.a(register_1_q), .b({5{1'b1}}), .eq(comparator_3_eq));  // open: gt, lt
  Multiplexer #(.width(8)) multiplexer_7 (
    .in0(motion_1_new_cords), .in1(x_q), .out(multiplexer_7_out), .sel(col));  // open: en
  nand nand_1 (nand_1_out, comparator_2_eq, comparator_1_gt);
  and and_1 (and_1_out, nand_1_out, nand_2_out);
  nand nand_2 (nand_2_out, comparator_3_eq, comparator_1_lt);
  Register register_2 (.D(multiplexer_7_out), .Q({out_8, register_2_q}), .clk(\reg ));  // open: en, clr
  check_collision check_collision_1 (
    .x(motion_1_new_cords), .y(motion_2_new_cords), .bat_left(5'b00011), .bat_right(5'b10001), .out_5(col));
  assign out_10 = and_1_out ? register_1_q : 5'bz;  // Controlled_Buffer controlled_buffer_3
  Register register_3 (.D(multiplexer_6_out), .Q({out_9, register_3_q}), .clk(\reg ));  // open: en, clr
  D_Flip_Flop d_ff_1 (.clk(aboba), .D(clock), .Q(d_ff_1_q));  // open: Qn, preset, en, reset
  D_Flip_Flop d_ff_2 (.clk(clock), .D(not_2_out), .Q(d_ff_2_q));  // open: Qn, preset, en, reset
  not not_1 (clock, d_ff_1_q);
  Bit_Extender #(.in_width(1), .out_width(5)) bit_extender_1 ();  // open: in, out
  not not_2 (not_2_out, d_ff_2_q);
  D_Flip_Flop d_ff_3 (.clk(not_2_out), .D(\reg ), .Q(d_ff_3_q));  // open: Qn, preset, en, reset
  D_Flip_Flop d_ff_4 (.clk(\reg ), .D(not_5_out), .Q(d_ff_4_q));  // open: Qn, preset, en, reset
  not not_3 (\reg , d_ff_3_q);
  D_Flip_Flop d_ff_5 (.clk(not_5_out), .D(not_4_out), .Q(d_ff_5_q));  // open: Qn, preset, en, reset
  not not_4 (not_4_out, d_ff_5_q);
  not not_5 (not_5_out, d_ff_4_q);
  and and_2 (and_2_out, not_6_out, p1g);
  not not_6 (not_6_out, col);
  Counter counter_1 (.Q(out_5), .clk(and_2_out), .clr(in_1));  // open: load, D, count, carry
  and and_3 (and_3_out, not_7_out, not_8_out, p2g);
  not not_7 (not_7_out, p1g);
  not not_8 (not_8_out, col);
  Counter counter_2 (.Q(out_6), .clk(and_3_out), .clr(in_1));  // open: load, D, count, carry

  assign out_7 = {5{1'b0}};
  assign out_11 = 5'b10001;

  // Other names for the same wires on the sheet: reset = in_1
endmodule

module reflect (
  input  [2:0] speed,
  input  cout,
  output [2:0] out_3,
  output out_4,
  output p2goal,
  output p1goal
);

  wire and_2_out, not_1_out;
  wire [2:0] negator_1_out;

  Negator #(.width(3)) negator_1 (.in(speed), .out(negator_1_out));
  xor xor_1 (out_4, speed[2], cout);
  Multiplexer #(.width(3)) multiplexer_1 (.in0(speed), .in1(negator_1_out), .out(out_3), .sel(out_4));  // open: en
  and and_1 (p2goal, out_4, speed[2]);
  and and_2 (and_2_out, out_4, cout);
  not not_1 (not_1_out, p2goal);
  and and_3 (p1goal, not_1_out, and_2_out);
endmodule

module motion (
  input  [7:0] coord,
  input  [2:0] speed,
  output [7:0] new_cords,
  output [2:0] new_speed,
  output p1goal,
  output p2goal
);

  wire adder_1_cout, reflect_1_out_4;
  wire [7:0] adder_1_out, bit_extender_1_out;

  assign bit_extender_1_out = {{5{speed[2]}}, speed};  // Bit_Extender bit_extender_1
  Adder adder_1 (.a(coord), .b(bit_extender_1_out), .out(adder_1_out), .cout(adder_1_cout));  // open: cin
  reflect reflect_1 (
    .speed(speed), .cout(adder_1_cout), .out_3(new_speed), .out_4(reflect_1_out_4), .p2goal(p2goal),
    .p1goal(p1goal));
  Multiplexer #(.width(8)) multiplexer_1 (
    .in0(adder_1_out), .in1(coord), .out(new_cords), .sel(reflect_1_out_4));  // open: en
endmodule

module check_collision (
  input  [7:0] x,
  input  [7:0] y,
  input  [4:0] bat_left,
  input  [4:0] bat_right,
  output out_5
);

  wire and_1_out, and_2_out, comparator_1_eq, comparator_2_eq, comparator_3_eq, comparator_4_eq,
       comparator_5_eq, comparator_6_eq, comparator_7_eq, comparator_8_eq, or_1_out, or_2_out;
  wire [4:0] inc_1_out_2, inc_2_out_2, inc_3_out_2, inc_4_out_2;

  inc inc_1 (.in_1(bat_right), .out_2(inc_1_out_2));
  inc inc_2 (.in_1(bat_left), .out_2(inc_2_out_2));
  inc inc_3 (.in_1(inc_2_out_2), .out_2(inc_3_out_2));
  inc inc_4 (.in_1(inc_1_out_2), .out_2(inc_4_out_2));
  Comparator #(.width(5)) comparator_1 (.a(y[7:3]), .b(bat_left), .eq(comparator_1_eq));  // open: gt, lt
  Comparator #(.width(5)) comparator_2 (.a(y[7:3]), .b(inc_2_out_2), .eq(comparator_2_eq));  // open: gt, lt
  Comparator #(.width(5)) comparator_3 (.a(y[7:3]), .b(inc_3_out_2), .eq(comparator_3_eq));  // open: gt, lt
  Comparator #(.width(5), .mode("unsigned")) comparator_4 (
    .a(x[7:3]), .b(5'b11100), .eq(comparator_4_eq));  // open: gt, lt
  Comparator #(.width(5)) comparator_5 (.a(y[7:3]), .b(bat_right), .eq(comparator_5_eq));  // open: gt, lt
  Comparator #(.width(5)) comparator_6 (.a(y[7:3]), .b(inc_1_out_2), .eq(comparator_6_eq));  // open: gt, lt
  Comparator #(.width(5)) comparator_7 (.a(y[7:3]), .b(inc_4_out_2), .eq(comparator_7_eq));  // open: gt, lt
  Comparator #(.width(5), .mode("unsigned")) comparator_8 (
    .a(x[7:3]), .b(5'b00011), .eq(comparator_8_eq));  // open: gt, lt
  or or_1 (or_1_out, comparator_1_eq, comparator_2_eq, comparator_3_eq);
  or or_2 (or_2_out, comparator_5_eq, comparator_6_eq, comparator_7_eq);
  and and_1 (and_1_out, comparator_8_eq, or_1_out);
  and and_2 (and_2_out, comparator_4_eq, or_2_out);
  or or_3 (out_5, and_1_out, and_2_out);

  // Other names for the same wires on the sheet: check = out_5
endmodule
